# Fritzing sketch pong (saved by Fritzing 0.9.3b)
breadboards: 1

parts:
  Part1 = Arduino Uno (Rev3)
  Nokia_5110_LCD_Module1 = Nokia 5110 LCD
  R1 = Rotary Potentiometer (Large) [maximum_resistance=100kΩ package=THT]
  R2 = Rotary Potentiometer (Large) [maximum_resistance=100kΩ package=THT]
  R3 = TRIMPOT [package=trimpot-3mm-2]
  J1 = Piezo Speaker
  R4 = Resistor [tolerance=±5% resistance=1k package=THT]
  R5 = Resistor [tolerance=±5% resistance=10k package=THT]
  R6 = Resistor [tolerance=±5% resistance=10k package=THT]
  R7 = Resistor [tolerance=±5% resistance=10k package=THT]
  R8 = Resistor [tolerance=±5% resistance=330 package=THT]
  R9 = Resistor [tolerance=±5% resistance=10k package=THT]
  R10 = Resistor [tolerance=±5% resistance=1k package=THT]

nets:
  N1: Part1.A0, R3.WIPER
  N2: Part1.A1, R2.wiper
  N3: Part1.A2, R1.wiper
  N4: Part1.D8, R8.Pin_1
  N5: Part1.D10_PWM/SS, R9.Pin_1
  N6: Part1.D11_PWM/MOSI, R7.Pin_1
  GND: Part1.GND, Nokia_5110_LCD_Module1.GND, Nokia_5110_LCD_Module1.GND_(out), R1.leg2, R2.leg2, R3.CW, R10.Pin_1
  3v3: Part1.AREF, Part1.3V3, Nokia_5110_LCD_Module1.VCC, Nokia_5110_LCD_Module1.VCC_(out), R1.leg1, R2.leg1, R3.CCW
  N7: Part1.D3_PWM, J1.pin2
  N8: Part1.D5_PWM, R6.Pin_1
  N9: Part1.D6_PWM, R5.Pin_1
  N10: Part1.D7, R4.Pin_1
  N11: Nokia_5110_LCD_Module1.SCE, Nokia_5110_LCD_Module1.SCE_(out), R4.Pin_0
  N12: Nokia_5110_LCD_Module1.RST, Nokia_5110_LCD_Module1.RST_(out), R5.Pin_0
  N13: Nokia_5110_LCD_Module1.D/C, Nokia_5110_LCD_Module1.D/C_(out), R6.Pin_0
  N14: Nokia_5110_LCD_Module1.DN(MOSI), Nokia_5110_LCD_Module1.DN(MODI)_(out), R7.Pin_0
  N15: Nokia_5110_LCD_Module1.SCLK, Nokia_5110_LCD_Module1.SCLK_(out), R9.Pin_0
  N16: Nokia_5110_LCD_Module1.LED, Nokia_5110_LCD_Module1.LED_(out), R8.Pin_0
  N17: J1.pin1, R10.Pin_0

notes:
  Player 1
  Player 2
  Contrast

custom parts:
  Nokia 5110 LCD: Nokia 5110 Graphic 84*48 LCD module such as the Sparkfun LCD-10168 or the clones from Ebay. There is example code for the Arduino available from the Sparkfun site in https://learn.sparkfun.com/tutorials/graphic-lcd-hookup-guide This is a 3.3V device, if you are running it from a 5V micro you need a 5V tolorant level translator such as the 74ahc367 to protect the signal imputs. Rafa G. did a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
